# Fritzing sketch DC_regulator (saved by Fritzing 0.9.3b)
breadboards: 1

parts:
  Dot_Matrix1 = LED Dot Matrix 18mm (0.7 INCH)  # not connected
  Q1 = Basic FET P-Channel [package="TO220 [THT]"]
  S1 = Momentary Switch [package=ksa_sealed_tac_switch]
  S2 = Momentary Switch [package=ksa_sealed_tac_switch]
  Часть1 = Arduino Uno (Rev3)
  R1 = Resistor [tolerance=±5% resistance=100k package=THT]
  R2 = Resistor [tolerance=±5% resistance=220 package=THT]
  R3 = Resistor [tolerance=±5% resistance=220 package=THT]
  D1 = Rectifier Diode [part_number=1N4001 package="300 mil [THT]"]  # not connected

nets:
  N1: Q1.gate, Часть1.A0
  N2: S1.2, S2.2, Часть1.5V
  N3: S1.4, Часть1.D8, R3.Pin_1
  N4: S2.4, Часть1.D9_PWM, R2.Pin_1
  N5: Часть1.GND, R1.Pin_1, R2.Pin_0

notes:
  +источника
  - источника
  GND VCC SDA SCL GND OUT
  Выходы цыфро-аналогового преобразователя MCP4725
  +5V
  -5V
